# Fritzing sketch demo-01 (saved by Fritzing 0.9.3b)
breadboards: 1

parts:
  Part1 = Arduino Uno (Rev3) - ICSP
  NEOPIXEL1 = Neopixel Strip -- White (30/m)
  R1 = Resistor [tolerance=±5% resistance=330 package=THT]

nets:
  N1: Part1.D3_PWM, R1.Pin_0
  5V: Part1.5V, NEOPIXEL1.+5V
  GND: Part1.GND, NEOPIXEL1.GND
  N2: NEOPIXEL1.Din, R1.Pin_1

custom parts:
  Neopixel Strip -- White (30/m): These NeoPixel strips have 30 digitally-addressable pixel LEDs per meter and are very affordable and are only 12.5 mm wide, 10 mm if you remove the strip from the casing.
